# Fritzing sketch sketsa sistem gas (saved by Fritzing 0.9.3b)
breadboards: 1

parts:
  U1 = NodeMCU V3.0
  Part1 = MQ-3 breakout
  J1 = Piezo Speaker
  LED1 = smd LED [color="Red (633nm)" package="1206 [SMD]"]
  J2 = Basic Servo
  Stromversorgung_Beradboard1 = Stromversorgung Beradboard [package=THT]

nets:
  3V3: U1.3V3, Part1.VCC
  VIN: U1.GND#6, U1.GND#13, U1.Vin, U1.GND#16, U1.GND#33, Part1.GND, J1.pin1, LED1.cathode, Stromversorgung_Beradboard1.+5_/_+3_Volt_4#13
  N1: U1.D5, J2.pulse
  N2: U1.D6, LED1.anode
  N3: U1.D7, J1.pin2
  N4: U1.A0, Part1.AO
  N5: J2.gnd, Stromversorgung_Beradboard1.Ground_1#14
  N6: J2.vcc, Stromversorgung_Beradboard1.+5_/_+3_Volt_4#12

custom parts:
  NodeMCU V3.0: ESP8266 based NodeMCU
  MQ-3 breakout: Alcohol sensor is capable of detecting alcohol (ethanol) particles on itself and gives the information in digital form back to us to manipulate with it. SKU:101251 • Voltage: 5V DC • Power: max 750mW • Measurement range: 0.04-4mg/L
